# Fritzing sketch Temp LCD and Flip Fritzing Diagram (saved by Fritzing 0.9.3b)
breadboards: 1

parts:
  DS1 = DS18B20 1-Wire Temperature Sensor Probe Cable
  LCD1 = LCD screen
  Parts1 = SparkFun RedBoard [part_number=DEV-12757]
  R1 = TRIMPOT [package=trimpot_pth_s3_lock]  # not connected
  U1 = BATTERY-2 [package=battery-aaa]  # not connected
  Part1 = Triple Axis Accelerometer Breakout - ADXL345
  R2 = Resistor [tolerance=±5% resistance=220 package=THT]
  R3 = Resistor [tolerance=±5% resistance=220 package=THT]

nets:
  GND: DS1.GND, LCD1.VSS, LCD1.R/W, LCD1.LED-, Parts1.GND, Part1.GND, Part1.INT2
  VDD: DS1.VDD, Parts1.3V3, Part1.VCC, Part1.CS, R2.Pin_1, R3.Pin_1
  N1: DS1.shield, Parts1.D7
  VDD_2: LCD1.VDD, LCD1.LED+, Parts1.5V
  N2: LCD1.RS, Parts1.D12/MISO
  N3: LCD1.E, Parts1.D11_PWM/MOSI
  N4: LCD1.DB4, Parts1.D5_PWM
  N5: LCD1.DB5, Parts1.D4
  N6: LCD1.DB6, Parts1.D3_PWM
  N7: LCD1.DB7, Parts1.D2
  N8: Parts1.A4/SDA, Part1.SDA, R2.Pin_0
  N9: Parts1.A5/SCL, Part1.SDO, R3.Pin_0

custom parts:
  LCD screen: A standard character display, usually with 2x16 characters. Comes in many colors.
  SparkFun RedBoard: At SparkFun we use many Arduinos and we’re always looking for the simplest, most stable one. Each board is a bit different and no one board has everything we want, so we decided to make our own version that combines all our favorite features. The RedBoard combines the simplicity of the UNO’s Optiboot bootloader (which is used in the Pro series), the stability of the FTDI (which we all missed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
